// Digital circuit Template.dig as structural Verilog
module Template (
  input  A,
  input  B,
  input  C,
  input  D,
  output Z1,
  output Z2,
  output Z3
);

  wire and_1_out, and_2_out, not_1_out, not_2_out, not_3_out, not_4_out, or_1_out, or_2_out, or_3_out,
       or_4_out, or_5_out, or_6_out, or_7_out, or_8_out, or_9_out;

  not not_1 (not_1_out, A);
  not not_2 (not_2_out, B);
  not not_3 (not_3_out, C);
  not not_4 (not_4_out, D);
  or or_1 (or_1_out, not_1_out, B, not_3_out, not_4_out);
  or or_2 (or_2_out, A, not_2_out, not_3_out, not_4_out);
  or or_3 (or_3_out, A, not_3_out, D);
  or or_4 (or_4_out, A, B, not_4_out);
  or or_5 (or_5_out, not_1_out, B, C);
  or or_6 (or_6_out, not_1_out, not_2_out, D);
  or or_7 (or_7_out, not_1_out, not_2_out, C, not_4_out);
  or or_8 (or_8_out, A, not_2_out, C, D);
  and and_1 (and_1_out, or_5_out, or_6_out, or_7_out, or_8_out);
  and and_2 (and_2_out, or_1_out, or_2_out, or_3_out, or_4_out);
  not not_5 (Z1, and_1_out);
  not not_6 (Z2, and_2_out);
  or or_9 (or_9_out, Z2, Z1);
  not not_7 (Z3, or_9_out);
endmodule
