// Digital circuit 01.dig as structural Verilog
module _01 (
  input  [3:0] In,
  output A,
  output B,
  output C,
  output D,
  output E,
  output F,
  output G
);

  wire nand_1_out, nand_2_out, nand_3_out, nand_4_out, nand_6_out, nand_7_out, nand_8_out, nand_9_out,
       nand_10_out, nand_11_out, nand_12_out, nand_13_out, nand_14_out, nand_15_out, not_1_out, not_2_out,
       not_3_out, not_4_out;

  not not_1 (not_1_out, In[3]);
  not not_2 (not_2_out, In[2]);
  not not_3 (not_3_out, In[1]);
  not not_4 (not_4_out, In[0]);
  nand nand_1 (nand_1_out, not_2_out, not_4_out);
  nand nand_2 (nand_2_out, In[2], In[0]);
  nand nand_3 (nand_3_out, not_3_out, not_4_out);
  nand nand_4 (nand_4_out, In[1], In[0]);
  nand nand_5 (C, not_2_out, In[1], not_4_out);
  nand nand_6 (nand_6_out, not_2_out, not_4_out);
  nand nand_7 (nand_7_out, not_2_out, In[1]);
  nand nand_8 (nand_8_out, In[2], not_3_out, In[0]);
  nand nand_9 (nand_9_out, In[1], not_4_out);
  nand nand_10 (nand_10_out, not_2_out, not_4_out);
  nand nand_11 (nand_11_out, In[1], not_4_out);
  nand nand_12 (nand_12_out, not_3_out, not_4_out);
  nand nand_13 (nand_13_out, not_2_out, In[1]);
  nand nand_14 (nand_14_out, In[2], not_3_out);
  nand nand_15 (nand_15_out, In[1], not_4_out);
  nand nand_16 (A, not_1_out, nand_1_out, nand_2_out, not_3_out);
  nand nand_17 (B, In[2], nand_3_out, nand_4_out);
  nand nand_18 (D, not_1_out, nand_6_out, nand_7_out, nand_8_out, nand_9_out);
  nand nand_19 (E, nand_10_out, nand_11_out);
  nand nand_20 (F, not_1_out, not_2_out, nand_12_out);
  nand nand_21 (G, not_1_out, nand_13_out, nand_14_out, nand_15_out);
endmodule
