// Digital circuit 011.dig as structural Verilog
module _011 (
  input  [3:0] In,
  output A
);

  wire not_1_out, not_2_out, not_3_out, not_4_out, or_1_out, or_2_out;

  not not_1 (not_1_out, In[3]);
  not not_2 (not_2_out, In[2]);
  not not_3 (not_3_out, In[1]);
  not not_4 (not_4_out, In[0]);
  or or_1 (or_1_out, In[3], In[2], In[1], In[0]);
  or or_2 (or_2_out, In[3], In[1], In[0], not_2_out);
  // Or or_3 has open pins: In_1=In[3], In_2=In[2], In_3=open, In_4=open, out=open
  // Or or_4 is placed but not wired
  nand nand_1 (A, or_1_out, or_2_out);
endmodule
