// Digital circuit lookup.digb.dig as structural Verilog
module lookup_digb (
  input  [3:0] in_1,
  output [3:0] out_2
);

  LookUpTable #(.Bits(4)) lookuptable_1 (.in0(in_1[0]), .in1(in_1[1]), .in2(in_1[2]), .in3(in_1[3]), .out(out_2));

  // Notes on the sheet:
  //   contents of lookuptable_1 (hex, n*v repeats v):
  //   0,1,2,3,4,5,6,7,8,9,a,b,c,d,e,f
endmodule
