// Digital circuit lookup_2.dig as structural Verilog
module lookup_2 (
  input  [3:0] Input,
  output [3:0] out_2
);

  LookUpTable #(.Bits(4)) lookuptable_1 (.in0(Input[0]), .in1(Input[1]), .in2(Input[2]), .in3(Input[3]), .out(out_2));

  // Other names for the same wires on the sheet: _0 = Input[0]; _1 = Input[1]; _2 = Input[2]; _3 = Input[3]

  // Notes on the sheet:
  //   contents of lookuptable_1 (hex, n*v repeats v):
  //   3,4,5,6,7,8,9,a,b,c,0,0,0,10
endmodule
