// Digital circuit 1.dig as structural Verilog
module _1 (
  input  Load,
  input  A,
  output Z
);

  wire driverinvsel_1_out, not_1_out, not_2_out;

  not not_1 (not_1_out, Load);
  assign driverinvsel_1_out = ~not_1_out ? A : 1'bz;  // DriverInvSel driverinvsel_1
  DriverInvSel driverinvsel_2 (.in(Z), .en(Load));  // open: out
  not not_2 (not_2_out, driverinvsel_1_out);
  not not_3 (Z, not_2_out);
endmodule
