// Digital circuit Template.dig as structural Verilog
module Template (
  input  J,
  input  K,
  input  Clear,
  input  Clock,
  output Q,
  output Q_2
);

  wire and_1_out, and_2_out, and_3_out, and_4_out, not_1_out, rs_ff_as_1_nq, rs_ff_as_1_q;

  and and_1 (and_1_out, Q_2, K, Clock);
  and and_2 (and_2_out, Clock, J, Q);
  RS_FF_AS rs_ff_as_1 (.S(and_2_out), .R(and_1_out), .Q(rs_ff_as_1_q), .nQ(rs_ff_as_1_nq));
  not not_1 (not_1_out, Clock);
  and and_3 (and_3_out, not_1_out, rs_ff_as_1_nq);
  and and_4 (and_4_out, rs_ff_as_1_q, not_1_out);
  RS_FF_AS rs_ff_as_2 (.S(and_4_out), .R(and_3_out), .Q(Q_2), .nQ(Q));
endmodule
