// Digital circuit Template.dig as structural Verilog
module Template (
  input  T,
  input  Clear,
  input  Clock,
  output Q,
  output Q_2
);

  wire and_1_out, and_2_out, and_3_out, and_4_out, nor_1_out, nor_2_out, not_1_out, not_2_out;

  not not_1 (not_1_out, Clock);
  and and_1 (and_1_out, Q_2, T, not_1_out);
  and and_2 (and_2_out, not_1_out, T, Q);
  nor nor_1 (nor_1_out, and_1_out, nor_2_out);
  nor nor_2 (nor_2_out, nor_1_out, Clear, and_2_out);
  not not_2 (not_2_out, not_1_out);
  and and_3 (and_3_out, not_2_out, nor_1_out);
  and and_4 (and_4_out, nor_2_out, not_2_out);
  nor nor_3 (Q, and_3_out, Q_2);
  nor nor_4 (Q_2, Q, and_4_out);
endmodule
