// Digital circuit template.dig as structural Verilog
module template (
  input  reset,
  input  clk,
  output A,
  output B,
  output C
);

  D_FF d_ff_1 (.D(reset), .C(clk), .Q(A));  // open: nQ
  D_FF d_ff_2 (.D(A), .C(clk), .Q(B));  // open: nQ
  D_FF d_ff_3 (.D(B), .C(clk), .Q(reset));  // open: nQ

  assign C = reset;
endmodule
